# Fritzing sketch Taller IoT (saved by Fritzing 0.9.2b)
breadboards: 1

parts:
  Parte1 = Arduino Uno (Rev3)
  R1 = Resistor [tolerance=±5% resistance=220 package="0402 [SMD]"]
  R2 = Resistor [tolerance=±5% resistance=220 package="0402 [SMD]"]
  LED1 = LED - 3mm [color="Red (633nm)" package="3 mm [THT]"]
  LED2 = LED - 3mm [color="Green (570nm)" package="3 mm [THT]"]
  S1 = SWITCH-MOMENTARY-2 [package=tactile-pth]
  U1 = TMP36 [package=to-92]
  R3 = Rotary Potentiometer (Small) [maximum_resistance=100kΩ package=THT]
  J1 = Basic Servo

nets:
  N1: Parte1.A0, U1.VOUT
  N2: Parte1.A1, R3.wiper
  N3: Parte1.D8, LED2.anode
  N4: Parte1.D9_PWM, J1.pulse
  N5: Parte1.D6_PWM, S1.2
  N6: Parte1.D7, R1.Pin_1, LED1.anode
  VCC: Parte1.5V, U1.VCC, R3.leg1, J1.vcc
  GND: Parte1.GND, R1.Pin_0, R2.Pin_0, S1.1, U1.GND, R3.leg2, J1.gnd
  N7: R2.Pin_1, LED2.cathode
